# Fritzing sketch electronics (saved by Fritzing 0.9.2b)
circuit board: 9.2cm x 6cm
breadboards: 2

parts:
  U1 = ATMEGA2560 [package=tqfp]
  XTAL1 = Crystal [frequency="16 Mhz" package=THT]
  C1 = Ceramic Capacitor [capacitance=10pF package="1206 [SMD, multilayer]"]
  C2 = Ceramic Capacitor [capacitance=10pF package="1206 [SMD, multilayer]"]
  IC3 = Voltage Regulator [package=78xxl]
  C7 = Electrolytic Capacitor [capacitance=10µF package="100 mil [THT, electrolytic]"]
  C8 = Electrolytic Capacitor [capacitance=10µF package="100 mil [THT, electrolytic]"]
  BATT1 = 4xAA Switchable Battery Pack w/Bare Wire
  R1 = Resistor [tolerance=±5% resistance=10k package="0402 [SMD]"]
  U3 = SD_CARD_SOCKET [package=sdcard_4uconn]
  IC4 = '4050 Hex Buffer
  C9 = Electrolytic Capacitor [capacitance=10µF package="100 mil [THT, electrolytic]"]
  C10 = Electrolytic Capacitor [capacitance=10µF package="100 mil [THT, electrolytic]"]
  IC5 = V_REG_LD1117VXX [package=78xxl]
  BAT1 = Battery Holders [package=battcon_12mm_pth]
  Y1 = CRYSTAL [package=crystal-32khz-smd]
  TFT1 = 2.2" TFT with MicroSD Breakout
  R4 = Resistor [tolerance=±5% resistance=2.2k package="0603 [SMD]"]
  R3 = Resistor [tolerance=±5% resistance=2.2k package="0603 [SMD]"]
  J1 = AVR ISP 6 Pin [package=2x3_offset]
  U4 = Header 8 [package=1x08_smd]
  IC6 = DS1307 [package=THT]

nets:
  N1: U1.(OC3A_AIN1)PE3, IC4.A
  N2: U1.(OC3C_INT5)PE5, TFT1.BL
  VCC: U1.VCC, U1.VCC1, U1.VCC2, U1.VCC3, U1.AREF, U1.AVCC, IC3.OUT, C8.+, R1.Pin_0, C10.+, IC5.IN, TFT1.VIN, R4.Pin_1, R3.Pin_1, J1.2, IC6.+V
  GND: U1.GND, U1.GND1, U1.GND2, U1.GND3, U1.AGND, C1.0, C2.0, IC3.GND, C7.-, C8.-, BATT1.NEG, U3.SH, U3.VSS1, U3.VSS2, IC4.VSS, C9.-, C10.-, IC5.GND, BAT1.-, TFT1.GND, J1.6, IC6.0V
  N3: U1.(SCK_PCINT1)PB1, IC4.C, TFT1.SCK, J1.3
  N4: U1.(MOSI_PCINT2)PB2, IC4.B, TFT1.MOSI, J1.4
  N5: U1.(MISO_PCINT3)PB3, U3.DAT0, TFT1.MISO, J1.1
  N6: U1.(OC2A_PCINT4)PB4, TFT1.CS
  N7: U1.(OC1A_PCINT5)PB5, TFT1.SDCS
  N8: U1.(OC1B_PCINT6)PB6, TFT1.RST
  N9: U1.RESET, R1.Pin_1, J1.5
  N10: U1.XTAL2, XTAL1.pin_0, C1.1
  N11: U1.XTAL1, XTAL1.pin_1, C2.1
  N12: U1.(SCL_INT0)PD0, R4.Pin_0, IC6.SCL_-_I2C_Clock
  N13: U1.(SDA_INT1)PD1, R3.Pin_0, IC6.SDA_-_I2C_Data
  N14: U1.(A13)PC5, U4.7
  N15: U1.(A14)PC6, U4.8
  N16: U1.(A15)PC7, U4.5
  N17: U1.(AD7)PA7, U4.6
  N18: U1.(AD6)PA6, U4.3
  N19: U1.(AD5)PA5, U4.4
  N20: U1.(AD4)PA4, U4.2
  N21: U1.(AD3)PA3, U4.1
  N22: IC3.IN, C7.+, BATT1.POS
  N23: U3.CD_DAT3, IC4.G
  N24: U3.CMD, IC4.H
  VDD: U3.VDD, IC4.VCC, C9.+, IC5.OUT
  N25: U3.CLK, IC4.I
  N26: BAT1.+, IC6.Vbat_-_Backup_Supply
  N27: Y1.1, IC6.X2_-_Crystal
  N28: Y1.2, IC6.X1_-_Crystal

custom parts:
  4xAA Switchable Battery Pack w/Bare Wire: 4xAA Switchable Battery Pack with Bare Wire connection
  2.2" TFT with MicroSD Breakout: 2.2" TFT Display with HX8340B Controller and MicroSD Card
